# Fritzing sketch Schaltplan GPS Uhr (saved by Fritzing 0.9.3b)

parts:
  Bauteil1 = Arduino Uno (Rev3)
  LCD1 = LCD screen
  SW2 = ENCODER_RGB_CA [package=encoder_led_3]

nets:
  N1: Bauteil1.A5/SCL, SW2.-G
  N2: Bauteil1.D9_PWM, LCD1.DB4
  N3: Bauteil1.D10_PWM/SS, LCD1.DB5
  N4: Bauteil1.D11_PWM/MOSI, LCD1.DB6
  N5: Bauteil1.D12/MISO, LCD1.DB7
  N6: Bauteil1.D2, SW2.SW
  N7: Bauteil1.D3_PWM, LCD1.RS
  N8: Bauteil1.D5_PWM, LCD1.E
  5V: Bauteil1.5V, LCD1.VDD, LCD1.LED+
  N9: Bauteil1.GND, SW2.-R
  N10: LCD1.VSS, LCD1.R/W, LCD1.LED-

notes:
  K
  A
  D7
  D6
  D5
  D4
  D3
  D2
  D1
  D0
  E
  RW
  RS
  V0
  VDD
  VSS
  GND + SW DT CLK
  VCC RX TX GND
