# Fritzing sketch Schaltplan GPS Uhr (saved by Fritzing 0.9.3b)

parts:
  LCD1 = LCD screen
  SW2 = ENCODER_RGB_CA [package=encoder_led_3]
  Bauteil1 = Arduino Uno (Rev3)
  R1 = Resistor [tolerance=±5% resistance=1k package=THT]

nets:
  VSS: LCD1.VSS, LCD1.R/W, LCD1.LED-, Bauteil1.GND, R1.Pin_1
  VDD: LCD1.VDD, LCD1.LED+, SW2.-R, Bauteil1.5V
  N1: LCD1.V0, Bauteil1.D4
  N2: LCD1.E, Bauteil1.D5_PWM
  N3: LCD1.DB4, Bauteil1.D9_PWM
  N4: LCD1.DB5, Bauteil1.D10_PWM/SS
  N5: LCD1.DB6, Bauteil1.D11_PWM/MOSI
  N6: LCD1.DB7, Bauteil1.D12/MISO
  N7: SW2.-G, Bauteil1.A5/SCL
  N8: SW2.SW, Bauteil1.D2

notes:
  D4
  D3
  D2
  D1
  D0
  E
  RW
  RS
  V0
  VDD
  VSS
  GND + SW DT CLK
  VCC RX TX GND
